# Fritzing sketch gps (saved by Fritzing 0.9.3b)
breadboards: 1

parts:
  Part1 = Arduino Nano (Rev3.0)
  neo-7m1 = NEO-7M [package=neo-7m]
  Part2 = Adafruit MicroSD card breakout board [part_number="Adafruit #254"]
  LED1 = smd LED [color="Orange (605nm)" package="1206 [SMD]"]
  LED2 = smd LED [color="Green (555nm)" package="1206 [SMD]"]
  R2 = Resistor [tolerance=±5% resistance=220 package=THT]
  R3 = Resistor [tolerance=±5% resistance=220 package=THT]

nets:
  GND: Part1.GND, neo-7m1.GND, Part2.GND, LED1.cathode, LED2.cathode
  N1: Part1.D2, neo-7m1.TXD
  N2: Part1.D3, neo-7m1.RXD
  N3: Part1.D6, R2.Pin_1
  N4: Part1.D9, R3.Pin_1
  N5: Part1.D10, Part2.CS
  N6: Part1.D11/MOSI, Part2.DI
  N7: Part1.D12/MISO, Part2.DO
  VCC: Part1.5V, neo-7m1.VCC, Part2.VCC
  3V3: Part1.3V3, Part2.+3V3
  N8: Part1.D13/SCK, Part2.CLK
  N9: LED1.anode, R2.Pin_0
  N10: LED2.anode, R3.Pin_0

custom parts:
  NEO-7M: NEO-7M GPS module
  Adafruit MicroSD card breakout board: Not just a simple breakout board, this microSD adapter goes the extra mile - designed for ease of use. Onboard 5v->3v regulator provides 150mA for power-hungry cards 3v level shifting means you can use this with ease on either 3v or 5v systems Uses a proper level shifting chip, not resistors: less problems, and faster read/write access Use 3 or 4 digital pins to read and write 2Gb+ of storage!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
